# Fritzing sketch Arduino_Circuit (saved by Fritzing 0.9.2b)
breadboards: 1

parts:
  Part1 = Arduino Nano (Rev3.0)
  Part2 = Bluetooth HC-06
  L30 = SMD RGB LED (WS2812B) [package=5050]
  Q1 = MOSFET-NCHANNEL [package=to220v]
  R1 = Resistor [tolerance=±5% resistance=220 package=THT]

nets:
  GND: Part1.GND, Part2.GND, Q1.S, R1.Pin_0
  N1: Part1.D3, Part2.TXD
  N2: Part1.D4, Part2.RXD
  N3: Part1.D10, Q1.G, R1.Pin_1
  5V: Part1.5V, Part2.VCC
  N4: L30.DOut, L30.VDD, Q1.D
  N5: L30.DIn, L30.VSS

custom parts:
  SMD RGB LED (WS2812B): The WS2812B is an RGB LED with a WS2811 control IC built right into the LED. Its improvement over its WS2812 ancestor is the reduction to 4 pins (a single power supply instead of 2) and dropping the requirement for the external resistors. The manufacturer says it has a better reverse connect protection.
